# Fritzing sketch Weather Station (saved by Fritzing 0.9.6b)
circuit board: 8.46667cm x 5.64444cm
breadboards: 1

parts:
  RHT1 = Humidity and Temperature Sensor RHT03
  Part1 = Arduino Uno (Rev3)
  R1 = Resistor [tolerance=±5% power=0.25 resistance=10k package=THT]
  Part2 = Barometric Pressure Sensor - BMP180 Breakout (GY-68)

nets:
  VCC: RHT1.Vcc, Part1.5V, R1.Pin_0, Part2.VCC
  N1: RHT1.Data-signal, Part1.D2, R1.Pin_1
  GND: RHT1.GND_2, Part1.GND, Part2.GND
  N2: Part1.A4/SDA, Part2.SDA
  N3: Part1.A5/SCL, Part2.SCL
